# Fritzing sketch fritzing client (saved by Fritzing 0.9.3b)

parts:
  U1 = ESP8266 NodeMCU LoLin module
  A1 = Arduino Nano Every THT
  negative = female pin header, 2 pins [form="♀ (female)"]
  J3 = female pin header, 2 pins [form="♀ (female)"]  # not connected
  J4 = female pin header, 2 pins [form="♀ (female)"]
  J5 = female pin header, 2 pins [form="♀ (female)"]
  J6 = female pin header, 2 pins [form="♀ (female)"]
  J7 = female pin header, 2 pins [form="♀ (female)"]  # not connected
  J8 = female pin header, 2 pins [form="♀ (female)"]  # not connected
  J9 = female pin header, 2 pins [form="♀ (female)"]
  J10 = female pin header, 2 pins [form="♀ (female)"]
  U2 = WS2812 RGB LED matrix 8x8

nets:
  N1: U1.D3, A1.Pin_21
  N2: U1.D4, A1.Pin_22
  N3: U1.Vin, J9.pin1
  N4: U1.GND, negative.pin1, negative.pin2, J5.pin1
  N5: A1.Pin_14, J4.pin2
  N6: A1.Pin_15, J6.pin2
  N7: A1.Pin_24, J10.pin2
  N8: J4.pin1, U2.GND
  N9: J6.pin1, U2.VCC
  N10: J10.pin1, U2.DIN

custom parts:
  ESP8266 NodeMCU LoLin module: ESP8266 based NodeMCU
  Arduino Nano Every THT: The Nano Every is Arduino’s 5V compatible board in the smallest available form factor: 45x18mm! The Arduino Nano is the preferred board for many projects requiring a small and easy to use microcontroller board. The small footprint and low price, make the Nano Every particularly suited for wearable inventions, low cost robotics, electronic musical instruments, and general use to control smaller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
  WS2812 RGB LED matrix 8x8: WS2812 matrix 8x8
