# Fritzing sketch fritzing server (saved by Fritzing 0.9.3b)

parts:
  U1 = ESP8266 NodeMCU LoLin module
  GY1 = MPU-6050 Board GY-521 [form="♀ (female)" package=THT]
  S1 = Toggle Switch [package=THT]
  S4 = Toggle Switch [package=THT]
  S5 = Toggle Switch [package=THT]
  J1 = female pin header, 2 pins [form="♀ (female)"]
  J2 = female pin header, 2 pins [form="♀ (female)"]
  J3 = female pin header, 2 pins [form="♀ (female)"]  # not connected
  J4 = female pin header, 2 pins [form="♀ (female)"]
  J5 = female pin header, 2 pins [form="♀ (female)"]
  J6 = female pin header, 2 pins [form="♀ (female)"]
  J7 = female pin header, 2 pins [form="♀ (female)"]  # not connected
  J8 = female pin header, 2 pins [form="♀ (female)"]  # not connected

nets:
  N1: U1.D1, GY1.pin3
  N2: U1.D2, GY1.pin4
  N3: U1.3V3, GY1.pin1
  N4: U1.GND, GY1.pin2, J4.pin1
  N5: U1.D6, S1.COM
  N6: U1.D7, S5.COM
  N7: U1.D8, S4.COM
  N8: U1.Vin, J6.pin2
  N9: S1.L1, J6.pin1
  N10: S1.L2, J2.pin2
  N11: S4.L1, J5.pin1
  N12: S4.L2, J1.pin2
  N13: S5.L1, J5.pin2
  N14: S5.L2, J2.pin1

custom parts:
  ESP8266 NodeMCU LoLin module: ESP8266 based NodeMCU
  MPU-6050 Board GY-521: Acelerometro y Giroscopio MPU-6050 Board GY-521
